// Logisim project IT012_Lab01_25520737.circ as structural Verilog: 5 circuits, main circuit TN1
module TN1 (
  input  A,
  input  B,
  input  C,
  output A_prime,
  output AB,
  output A_B,
  output AB__prime,
  output CHAIN,
  output A_B_2,
  output A_B__prime,
  output A_B__prime_2,
  output XOR3,
  output NAND3
);

  not not_1 (A_prime, A);
  and and_1 (AB, A, B);
  or or_1 (A_B, A, B);
  nand nand_1 (AB__prime, A, B);
  xor xor_1 (A_B_2, A, B);
  xnor xnor_1 (A_B__prime, A, B);
  nor nor_1 (A_B__prime_2, A, B);
  ExactlyOne xor_2 (.out(XOR3), .in0(A), .in2(B), .in4(C));
  nand nand_2 (NAND3, A, B, C);
  nand nand_3 (CHAIN, AB__prime, C);
endmodule

module TN2 (
  input  x,
  input  y,
  input  z,
  output EQ1,
  output EQ2,
  output EQ3,
  output EQ4,
  output EQ5
);

  wire and_1_out, and_2_out, and_3_out, and_4_out, nand_1_out, nor_1_out, not_1_out, not_2_out, or_1_out,
       or_2_out, or_3_out, or_4_out, or_5_out;

  not not_1 (not_1_out, x);
  not not_2 (not_2_out, y);
  and and_1 (and_1_out, not_1_out, y);
  and and_2 (and_2_out, y, z);
  or or_1 (or_1_out, x, z);
  or or_2 (or_2_out, x, y);
  nor nor_1 (nor_1_out, x, y);
  and and_3 (and_3_out, not_1_out, not_2_out);
  nand nand_1 (nand_1_out, x, y);
  or or_3 (or_3_out, x, and_2_out);
  and and_4 (and_4_out, or_1_out, or_2_out);
  or or_4 (or_4_out, x, and_1_out);
  or or_5 (or_5_out, x, y);
  xnor xnor_1 (EQ1, nor_1_out, and_3_out);
  xnor xnor_2 (EQ2, and_3_out, nand_1_out);
  xnor xnor_3 (EQ3, or_3_out, and_4_out);
  xnor xnor_4 (EQ4, x, or_4_out);
  xnor xnor_5 (EQ5, or_4_out, or_5_out);
endmodule

module TN3 (
  input  A,
  input  B,
  input  C,
  input  D,
  output F
);

  wire m2_out, m3_out, m5_out, m7_out, m11_out, not_1_out, not_2_out, not_3_out, not_4_out;

  not not_1 (not_1_out, A);
  not not_2 (not_2_out, B);
  not not_3 (not_3_out, C);
  not not_4 (not_4_out, D);
  and m2 (m2_out, not_1_out, not_2_out, not_4_out);
  and m3 (m3_out, not_1_out, not_2_out, D);
  and m5 (m5_out, not_1_out, B, D);
  and m7 (m7_out, not_1_out, B, D);
  and m11 (m11_out, A, not_2_out, D);
  or or_1 (F, m2_out, m3_out, m5_out, m7_out, m11_out);
endmodule

module TN4 (
  input  A,
  input  B,
  input  C,
  input  D,
  output F_can,
  output EQ1,
  output F_sop,
  output EQ2,
  output F_pos
);

  wire and_1_out, m0_out, m1_out, m2_out, m3_out, m5_out, m7_out, m9_out, m11_out, not_1_out, not_2_out,
       not_3_out, not_4_out, or_1_out;

  not not_1 (not_1_out, A);
  not not_2 (not_2_out, B);
  not not_3 (not_3_out, C);
  not not_4 (not_4_out, D);
  and m0 (m0_out, not_1_out, not_2_out, not_3_out, not_4_out);
  and m2 (m2_out, not_1_out, not_2_out, not_4_out);
  and m3 (m3_out, not_1_out, not_2_out, D);
  and m5 (m5_out, not_1_out, B, D);
  and m7 (m7_out, not_1_out, B, D);
  and m11 (m11_out, A, not_2_out, D);
  and m1 (m1_out, not_1_out, not_2_out, not_3_out, D);
  and m9 (m9_out, not_2_out, not_3_out, A, D);
  and and_1 (and_1_out, not_1_out, not_2_out);
  or or_1 (or_1_out, not_1_out, not_2_out);
  or or_2 (F_sop, and_1_out, D);
  and and_2 (F_pos, or_1_out, D);
  or or_3 (F_can, m0_out, m2_out, m3_out, m5_out, m7_out, m11_out, m1_out, m9_out);
  xnor xnor_1 (EQ1, F_can, F_sop);
  xnor xnor_2 (EQ2, F_can, F_pos);
endmodule

module TN5 (
  input  A,
  input  B,
  input  C,
  output F
);

  wire xor_1_out;

  xor xor_1 (xor_1_out, A, B);
  xor xor_2 (F, xor_1_out, C);
endmodule
